// Logisim project ADDER.circ as structural Verilog: 1 circuit, main circuit main
module main (
  input  A,
  input  B,
  input  A_2,
  input  B_2,
  input  C,
  output SUM,
  output D,
  output S,
  output D_2
);

  wire and_2_out, and_3_out, xor_2_out;

  xor xor_1 (SUM, A, B);
  xor xor_2 (xor_2_out, A_2, B_2);
  and and_1 (D, A, B);
  xor xor_3 (S, xor_2_out, C);
  and and_2 (and_2_out, C, xor_2_out);
  and and_3 (and_3_out, B_2, A_2);
  buf or_1 (D_2, and_3_out);  // OR_Gate

  // Notes on the sheet:
  //   HALF ADDER 
  //   FULL ADDER 
  //   C
  //   CARRY 
  //   SUM
  //   CARRY 
endmodule
