// Logisim project BOOLEEN.circ as structural Verilog: 1 circuit, main circuit main
module main (
  input  B_A_C,
  input  in_2,
  input  in_3,
  output out_4
);

  wire or_1_out;

  or or_1 (or_1_out, B_A_C, in_2);
  and and_1 (out_4, or_1_out, in_3);

  // Notes on the sheet:
  //   AB +BC (B+C)
  //   AB+BBC+BCC
  //   AB+BC+BC
  //   AB+BC
endmodule
