// Logisim project SUBTRACTOR.circ as structural Verilog: 1 circuit, main circuit main
module main (
  input  A,
  input  B,
  input  C,
  input  A_2,
  input  B_2,
  output C_2,
  output D,
  output V,
  output U
);

  wire and_1_out, and_3_out, not_1_out, not_2_out, not_3_out, xor_2_out;

  not not_1 (not_1_out, A_2);
  xor xor_1 (C_2, A, B);
  not not_2 (not_2_out, A);
  xor xor_2 (xor_2_out, A_2, B_2);
  and and_1 (and_1_out, B_2, not_1_out);
  and and_2 (D, B, not_2_out);
  not not_3 (not_3_out, xor_2_out);
  xor xor_3 (V, C, xor_2_out);
  and and_3 (and_3_out, not_3_out, C);
  or or_1 (U, and_3_out, and_1_out);

  // Notes on the sheet:
  //   HALF SUBTRACTOR
  //   FULL SUBTRACTOR 
  //   DIFFERENCE 
  //   BORROW 
  //   DIFFERENCE 
  //   BORROW
endmodule
