// Logisim project VARIOUS GATE.circ as structural Verilog: 1 circuit, main circuit main
module main (
  input  A,
  input  R,
  input  B,
  input  S,
  input  P,
  input  V,
  input  Q,
  input  H,
  input  G,
  input  Y,
  input  Z,
  input  M,
  input  N,
  output C,
  output T,
  output U,
  output R_2,
  output F,
  output X,
  output O
);

  and and_1 (C, A, B);
  or or_1 (R_2, P, Q);
  nand nand_1 (F, H, G);
  nor nor_1 (X, Y, Z);
  xor xor_1 (O, M, N);
  xnor xnor_1 (T, R, S);
  not not_1 (U, V);

  // Notes on the sheet:
  //   AND GATE 
  //   OR GATE 
  //   NAND GATE 
  //   NOR GATE 
  //   XOR GATE 
  //   XNOR GATE 
  //   NOT GATE
endmodule
